// Logisim project FinalAssesments.circ as structural Verilog: 1 circuit, main circuit main
module main (
);

  wire and_1_out, and_2_out, and_3_out, and_4_out, and_5_out, and_6_out, and_7_out, and_8_out, and_9_out,
       and_10_out, and_11_out, and_12_out, and_13_out, and_14_out, and_15_out, and_16_out, and_17_out,
       and_18_out, and_19_out, button_1_out, clock_1_out, d_ff_1_q, d_ff_2_q, d_ff_3_q, d_ff_4_q, not_1_out,
       not_2_out, not_3_out, not_4_out, not_5_out, not_6_out, not_7_out, not_8_out, not_9_out, not_10_out,
       not_11_out, not_12_out, not_13_out, not_14_out, not_15_out, not_16_out, not_17_out, not_18_out,
       not_19_out, not_20_out, not_21_out, not_22_out, not_23_out, not_24_out, not_25_out, not_26_out,
       not_27_out, not_28_out, or_1_out, or_2_out, or_3_out, or_4_out, or_5_out, or_6_out, or_7_out, or_8_out;

  not not_1 (not_1_out, d_ff_1_q);
  not not_2 (not_2_out, d_ff_2_q);
  not not_3 (not_3_out, d_ff_3_q);
  not not_4 (not_4_out, d_ff_1_q);
  not not_5 (not_5_out, d_ff_3_q);
  not not_6 (not_6_out, d_ff_2_q);
  not not_7 (not_7_out, d_ff_3_q);
  not not_8 (not_8_out, d_ff_1_q);
  not not_9 (not_9_out, d_ff_3_q);
  not not_10 (not_10_out, d_ff_1_q);
  not not_11 (not_11_out, d_ff_2_q);
  not not_12 (not_12_out, d_ff_3_q);
  and and_1 (and_1_out, not_1_out, d_ff_2_q, d_ff_3_q, d_ff_4_q);
  and and_2 (and_2_out, d_ff_1_q, not_2_out, not_3_out, d_ff_4_q);
  and and_3 (and_3_out, not_4_out, not_5_out, d_ff_4_q);
  and and_4 (and_4_out, not_6_out, not_7_out, d_ff_4_q);
  and and_5 (and_5_out, not_8_out, d_ff_2_q, not_9_out, d_ff_4_q);
  not not_13 (not_13_out, d_ff_1_q);
  not not_14 (not_14_out, d_ff_2_q);
  not not_15 (not_15_out, d_ff_3_q);
  and and_6 (and_6_out, not_11_out, not_12_out, d_ff_4_q);
  Clock clock_1 (.out(clock_1_out));
  or or_1 (or_1_out, and_1_out, and_2_out);
  or or_2 (or_2_out, and_3_out, and_4_out);
  and and_7 (and_7_out, not_13_out, not_14_out, not_15_out);
  and and_8 (and_8_out, not_10_out, d_ff_2_q, d_ff_4_q);
  or or_3 (or_3_out, and_7_out, and_8_out, and_6_out);
  Button button_1 (.out(button_1_out));
  D_Flip_Flop d_ff_1 (.clk(clock_1_out), .D(or_1_out), .Q(d_ff_1_q), .reset(button_1_out));  // open: Qn, preset, en
  D_Flip_Flop d_ff_2 (.clk(clock_1_out), .D(or_2_out), .Q(d_ff_2_q), .reset(button_1_out));  // open: Qn, preset, en
  D_Flip_Flop d_ff_3 (.clk(clock_1_out), .D(and_5_out), .Q(d_ff_3_q), .reset(button_1_out));  // open: Qn, preset, en
  D_Flip_Flop d_ff_4 (.clk(clock_1_out), .D(or_3_out), .Q(d_ff_4_q), .reset(button_1_out));  // open: Qn, preset, en
  not not_16 (not_16_out, d_ff_1_q);
  not not_17 (not_17_out, d_ff_3_q);
  not not_18 (not_18_out, d_ff_2_q);
  not not_19 (not_19_out, d_ff_3_q);
  not not_20 (not_20_out, d_ff_1_q);
  not not_21 (not_21_out, d_ff_3_q);
  not not_22 (not_22_out, d_ff_1_q);
  not not_23 (not_23_out, d_ff_3_q);
  not not_24 (not_24_out, d_ff_1_q);
  not not_25 (not_25_out, d_ff_3_q);
  not not_26 (not_26_out, d_ff_1_q);
  and and_9 (and_9_out, not_26_out, d_ff_2_q, d_ff_4_q);
  not not_27 (not_27_out, d_ff_3_q);
  not not_28 (not_28_out, d_ff_1_q);
  and and_10 (and_10_out, not_16_out, d_ff_2_q, d_ff_4_q);
  and and_11 (and_11_out, d_ff_1_q, not_18_out, not_19_out, d_ff_4_q);
  and and_12 (and_12_out, not_20_out, not_21_out, d_ff_4_q);
  and and_13 (and_13_out, not_22_out, d_ff_2_q, d_ff_4_q);
  and and_14 (and_14_out, d_ff_2_q, not_17_out, d_ff_4_q);
  and and_15 (and_15_out, not_23_out, d_ff_4_q);
  and and_16 (and_16_out, not_24_out, d_ff_2_q, d_ff_4_q);
  and and_17 (and_17_out, d_ff_1_q, not_25_out, d_ff_4_q);
  and and_18 (and_18_out, d_ff_1_q, not_27_out, d_ff_4_q);
  or or_4 (or_4_out, and_10_out, and_11_out);
  or or_5 (or_5_out, and_12_out, and_13_out, and_14_out);
  or or_6 (or_6_out, and_15_out, and_16_out);
  and and_19 (and_19_out, not_28_out, d_ff_2_q, d_ff_3_q, d_ff_4_q);
  or or_7 (or_7_out, and_17_out, and_9_out);
  or or_8 (or_8_out, and_18_out, and_19_out);
  _7_Segment_Display u_7_segment_display_1 (
    .g(or_8_out), .f(or_7_out), .a(or_4_out), .b(or_5_out), .e(or_4_out), .d(or_4_out), .c(or_6_out));  // open: dp
endmodule
